# Fritzing sketch semaforo (saved by Fritzing 0.9.2b)
breadboards: 1

parts:
  Board1 = Arduino Uno (Rev3)
  LCD1 = LCD screen
  R2 = Rotary Potentiometer (Small) [maximum_resistance=100kΩ package=THT]
  LED1 = LED - 5mm [color="Red (633nm)" package="5 mm [THT]"]
  LED2 = LED - 5mm [color="Yellow (595nm)" package="5 mm [THT]"]
  LED3 = LED - 5mm [color="Green (570nm)" package="5 mm [THT]"]
  R3 = Resistor [tolerance=±5% resistance=220 package=THT]
  R4 = Resistor [tolerance=±5% resistance=220 package=THT]
  R5 = Resistor [tolerance=±5% resistance=220 package=THT]
  LED4 = LED - 5mm [color="Red (633nm)" package="5 mm [THT]"]
  LED5 = LED - 5mm [color="Yellow (595nm)" package="5 mm [THT]"]
  LED6 = LED - 5mm [color="Green (570nm)" package="5 mm [THT]"]
  R6 = Resistor [tolerance=±5% resistance=220 package=THT]
  R7 = Resistor [tolerance=±5% resistance=220 package=THT]
  R8 = Resistor [tolerance=±5% resistance=220 package=THT]
  R1 = Resistor [tolerance=±5% resistance=220 package=THT]

nets:
  N1: Board1.D8, LED1.anode
  VerdeF2: Board1.D9_PWM, LED6.anode
  AmarilloF2: Board1.D10_PWM/SS, LED5.anode
  N2: Board1.D11_PWM/MOSI, LCD1.E
  N3: Board1.D12/MISO, LCD1.RS
  RojoF2: Board1.D13/SCK, LED4.anode
  N4: Board1.D2, LCD1.DB7
  N5: Board1.D3_PWM, LCD1.DB6
  N6: Board1.D4, LCD1.DB5
  N7: Board1.D5_PWM, LCD1.DB4
  N8: Board1.D6_PWM, LED3.anode
  N9: Board1.D7, LED2.anode
  5V: Board1.5V, LCD1.VDD, R2.leg1, R1.Pin_1
  GND: Board1.GND, LCD1.VSS, LCD1.R/W, LCD1.LED-, R2.leg2, R3.Pin_0, R4.Pin_0, R5.Pin_0, R6.Pin_0, R7.Pin_0, R8.Pin_0
  N10: LCD1.V0, R2.wiper
  N11: LCD1.LED+, R1.Pin_0
  N12: LED1.cathode, R3.Pin_1
  N13: LED2.cathode, R4.Pin_1
  N14: LED3.cathode, R5.Pin_1
  N15: LED4.cathode, R6.Pin_1
  N16: LED5.cathode, R7.Pin_1
  N17: LED6.cathode, R8.Pin_1

notes:
  Fase 1
  Fase 2
  16x2
